# Fritzing sketch LCD (saved by Fritzing 0.9.2b)
breadboards: 1

parts:
  Part1 = Photon
  U1 = LCD-16X2 [package=lcd-16x2_noholes]

nets:
  GND: Part1.GND, U1.VSS, U1.VO, U1.R_W, U1.K
  VIN: Part1.VIN, U1.VDD, U1.A
  N1: Part1.D0, U1.RS
  N2: Part1.D1, U1.E
  N3: Part1.D2, U1.DB4
  N4: Part1.D3, U1.DB5
  N5: Part1.D4, U1.DB6
  N6: Part1.D5, U1.DB7
